// Logisim project Secret_Circuit.circ as structural Verilog: 1 circuit, main circuit main
module main (
  input  E_0,
  input  E_1,
  input  E_2,
  input  E_3,
  input  E_4,
  input  E_5,
  input  E_6,
  input  E_7,
  input  E_8,
  input  E_9
);

  wire and_1_out, and_2_out, and_3_out, and_4_out, and_5_out, and_6_out, and_7_out, and_8_out, and_9_out,
       nand_1_out, not_1_out, not_2_out, xor_1_out;

  and and_1 (and_1_out, E_0, E_1);
  not not_1 (not_1_out, E_2);
  and and_2 (and_2_out, E_6, E_7);
  not not_2 (not_2_out, E_8);
  and and_3 (and_3_out, and_1_out, not_1_out);
  xor xor_1 (xor_1_out, E_4, E_5);
  nand nand_1 (nand_1_out, not_1_out, E_3);
  and and_4 (and_4_out, E_5, and_2_out);
  and and_5 (and_5_out, not_2_out, E_9);
  and and_6 (and_6_out, and_3_out, and_7_out);
  and and_7 (and_7_out, nand_1_out, xor_1_out);
  and and_8 (and_8_out, and_4_out, and_5_out);
  and and_9 (and_9_out, and_6_out, and_8_out);
  LED led_1 (.in(and_9_out));
endmodule
