// Logisim project NSHA_64.circ as structural Verilog: 5 circuits, main circuit main
module main (
  input  [63:0] Message,
  input  [63:0] Cle_Secrete,
  output [63:0] result,
  output [15:0] nombre_cycle,
  output is_done
);

  wire bitselector_1_out, CLK, not_1_out, RST, secure_hash_1_is_done;
  wire [0:0] or_1_out;
  wire [3:0] bit_extender_1_out;
  wire [5:0] iterateur_1_s;
  wire [63:0] and_1_out;

  Clock u_CLK (.out(CLK));
  Button init (.out(RST));
  assign and_1_out = Message & Cle_Secrete;  // AND_Gate and_1, 64 bits wide
  BitSelector #(.width(64)) bitselector_1 (.in(and_1_out), .out(bitselector_1_out), .sel(iterateur_1_s));
  iterateur iterateur_1 (.INC({{5{1'b0}}, or_1_out[0]}), .CLK(CLK), .RST(RST), .S(iterateur_1_s));
  LED led_1 (.in(bitselector_1_out));
  Hex_Digit_Display hex_digit_display_1 (.value(bit_extender_1_out));  // open: dp
  assign bit_extender_1_out = {{2{1'b0}}, iterateur_1_s[5:4]};  // Bit_Extender bit_extender_1
  Comparator #(.width(6)) comparator_1 (.a(iterateur_1_s), .b({6{1'b1}}), .eq(is_done));  // open: gt, lt
  or or_1 (or_1_out[0], not_1_out, secure_hash_1_is_done);
  not not_1 (not_1_out, bitselector_1_out);
  Secure_Hash secure_hash_1 (
    .input_bit(bitselector_1_out), .CLK(CLK), .RST(RST), .is_done(secure_hash_1_is_done), .result(result));
  Compteur_cycle compteur_cycle_1 (.CLK(CLK), .RST(RST), .res(nombre_cycle));
  Hex_Digit_Display hex_digit_display_2 (.value(iterateur_1_s[3:0]));  // open: dp

  // Other names for the same wires on the sheet: KEY[63:0] = Cle_Secrete; MSG[63:0] = Message

  // Notes on the sheet:
  //   INPUTS
  //   CIRCUIT
endmodule

module iterateur (
  input  [5:0] INC,
  input  CLK,
  input  RST,
  output [5:0] S
);

  wire [5:0] adder_1_out;

  Register #(.width(6)) register_1 (.D(adder_1_out), .clk(CLK), .Q(S), .clr(RST));  // open: en
  Adder #(.width(6)) adder_1 (.a(S), .b(INC), .out(adder_1_out));  // open: cin, cout
endmodule

module Secure_Hash (
  input  input_bit,
  input  CLK,
  input  RST,
  output is_done,
  output [63:0] result
);

  wire and_1_out, bitselector_2_out, long_to_single_pulse_1_o, not_1_out, not_2_out;
  wire [5:0] bitselector_1_out, or_1_out;
  wire [63:0] adder_1_out, bit_extender_1_out, bit_extender_2_out, shifter_1_out, subtractor_1_out, xor_1_out;

  not not_1 (not_1_out, not_2_out);
  not not_2 (not_2_out, input_bit);
  assign bit_extender_1_out = {{63{1'b0}}, not_2_out};  // Bit_Extender bit_extender_1
  assign bit_extender_2_out = {{63{1'b0}}, input_bit};  // Bit_Extender bit_extender_2
  Subtractor #(.width(64)) subtractor_1 (
    .a(result), .b(bit_extender_1_out), .out(subtractor_1_out));  // open: bin, bout
  assign xor_1_out = subtractor_1_out ^ shifter_1_out;  // XOR_Gate xor_1, 64 bits wide
  BitSelector #(.group(6), .width(64)) bitselector_1 (.in(result), .out(bitselector_1_out), .sel(4'b0001));
  assign or_1_out = 6'b001111 | bitselector_1_out;  // OR_Gate or_1, 6 bits wide
  Adder #(.width(64)) adder_1 (.a(xor_1_out), .b(bit_extender_2_out), .out(adder_1_out));  // open: cin, cout
  Shifter #(.width(64)) shifter_1 (.in(result), .\dist (or_1_out), .out(shifter_1_out));
  Register #(.width(64)) register_1 (.D(adder_1_out), .clk(CLK), .Q(result), .clr(RST));  // open: en
  BitSelector #(.width(64)) bitselector_2 (.in(result), .out(bitselector_2_out), .sel(6'b000011));
  and and_1 (and_1_out, not_1_out, bitselector_2_out);
  LED led_1 (.in(bitselector_2_out));
  long_to_single_pulse long_to_single_pulse_1 (.i(and_1_out), .rst(RST), .clk(CLK), .o(long_to_single_pulse_1_o));
  and and_2 (is_done, long_to_single_pulse_1_o, input_bit);

  // Notes on the sheet:
  //   Un joli bordel
endmodule

module Compteur_cycle (
  input  CLK,
  input  RST,
  output [15:0] res
);

  wire [15:0] adder_1_out;

  Register #(.width(16)) register_1 (.D(adder_1_out), .clk(CLK), .Q(res), .clr(RST));  // open: en
  Adder #(.width(16)) adder_1 (.a(res), .b(16'h1), .out(adder_1_out));  // open: cin, cout
endmodule

module long_to_single_pulse (
  input  i,
  input  rst,
  input  clk,
  output o
);

  wire not_1_out, register_1_q, register_2_q, register_3_q;

  Register #(.width(1)) register_1 (.D(i), .clk(clk), .Q(register_1_q), .clr(rst));  // open: en
  Register #(.width(1)) register_2 (.D(i), .clk(clk), .Q(register_2_q), .clr(rst));  // open: en
  Register #(.width(1)) register_3 (.D(register_1_q), .clk(clk), .Q(register_3_q), .clr(rst));  // open: en
  not not_1 (not_1_out, register_3_q);
  and and_1 (o, register_2_q, not_1_out);
endmodule
